# Fritzing sketch GPS_ISS_WeMos_OLED (saved by Fritzing 0.9.3b)
breadboards: 1

parts:
  WeMos_D1_Mini1 = WeMos D1 Mini  # not connected
  OLED_I2C1 = OLED 128x64 I2C Monochrome Display
  M1 = NEO-6M GPS Module [part_number=GY-GPS6MV2]

nets:
  VDD: OLED_I2C1.VDD, M1.Vcc
  GND: OLED_I2C1.GND, M1.GND

custom parts:
  NEO-6M GPS Module: GY-GPS6MV2 NEO-6M GPS Module Module based on U-blox NEO-6M GPS engine, incorporating regulator for 3.3-5V DC input, MS621FE-compatible rechargeable battery for backup and EEPROM for storing configuration settings. Links: NEO-6 series product information page NEO-6 Datasheet
